# Fritzing sketch water pump (saved by Fritzing 0.9.3b)

parts:
  U2 = ESP8266 WiFi Module [part_number=ESP8266]
  VCC1 = 4 x AAA Battery Mount
  M1 = DC Motor
  U1 = V_REG_LD1117VXX [package=78xxl]
  WeMos_D1_Mini_Relay_Shield1 = WeMos D1 Mini Relay Shield V2
  Part1 = Soil Moisture Sensor
  R1 = Dial Potentiometer with switch [maximum_resistance=100kΩ]

nets:
  N1: U2.IO5, R1.wiper
  N2: U2.IO15, WeMos_D1_Mini_Relay_Shield1.D1
  GND: U2.GND, VCC1.-, M1.pin_1, U1.GND, WeMos_D1_Mini_Relay_Shield1.G, R1.switch_leg2
  N3: U2.3.3V, U1.OUT
  N4: VCC1.+, U1.IN, WeMos_D1_Mini_Relay_Shield1.5V, WeMos_D1_Mini_Relay_Shield1.COM, R1.leg2
  N5: M1.pin_2, WeMos_D1_Mini_Relay_Shield1.NO
  N6: Part1.SIG, R1.leg1
  N7: Part1.GND, R1.switch_leg1

notes:
  5v water pump
  5v Battery pack
  5v to 3.3v voltage step down regulator.
  1-Channel 5v Relay
  ESP8266-ESP01
  GPIO0- Soil moisture input
  GPIO2- Water pump relay
  This is going to be the sensor probe, with an adjustable sensitivity.
  https://circuitdigest.com/microcontroller-projects/interfacing-soil-moisture-sensor-with-arduino-uno#:~:text=The%20soil%20moisture%20sensor%20is,needed%2C%20avoiding%20overwatering%20and%20underwatering.
  https://circuitdigest.com/microcontroller-projects/interfacing-soil-moisture-sensor-with-arduino-uno#:~:text=The%20soil%20moisture%20sensor%20is,needed%2C%20avoiding%20overwatering%20and%20underwatering.
  Moisture Sensor
